# Fritzing sketch hardware_schematic (saved by Fritzing 1.0.3b)

parts:
  A1 = Micro SD card reader
  S1 = Round Pushbutton
  S2 = Round Pushbutton
  S3 = Round Pushbutton
  S4 = Round Pushbutton
  U1 = ESP8266 NodeMCU LoLin module

nets:
  N1: A1.Pin_1, U1.3V3
  N2: A1.Pin_2, U1.D8
  N3: A1.Pin_3, U1.D7
  N4: A1.Pin_4, U1.D5
  N5: A1.Pin_5, U1.D6
  N6: A1.Pin_6, S1.leg1, S2.leg1, S3.leg1, S4.leg1, U1.GND
  N7: S1.leg0, U1.D1
  N8: S2.leg0, U1.D2
  N9: S3.leg0, U1.D3
  N10: S4.leg0, U1.D4

custom parts:
  Micro SD card reader: Micro SD card reader.
  ESP8266 NodeMCU LoLin module: ESP8266 based NodeMCU
